# Fritzing sketch IR Proximity Sensor (saved by Fritzing 0.9.10b)
breadboards: 1

parts:
  U1 = LM358 [package=dip08]
  R1 = Resistor [tolerance=±5% power=0.25 resistance=10k package=THT]
  R2 = Resistor [tolerance=±5% power=0.25 resistance=270 package=THT]
  LED1 = LED - 5mm [color="Red (633nm)" current=0.030 package="5 mm [THT]"]
  LED2 = LED - 5mm [color="Red (633nm)" current=0.030 package="5 mm [THT]"]
  U2 = POT [knob_status=50% power=0.5W package=3362u]
  LED3 = LEDs [package=led10mm]
  R3 = Resistor [tolerance=±5% power=0.25 resistance=220 package=THT]
  VCC1 = Battery block 9V

nets:
  N1: U1.G$1_OUT, LED3.A
  N2: U1.G$1_-IN, U2.S
  N3: U1.G$1_+IN, R1.Pin_1, LED1.cathode
  N4: U1.G$1_V-, U2.E
  N5: U1.G$1_V+, LED1.anode, LED2.cathode, U2.A, VCC1.+
  N6: R1.Pin_0, R2.Pin_0, VCC1.-
  N7: R2.Pin_1, LED2.anode
  N8: LED3.C, R3.Pin_0

notes:
  First Project
  IR Proximity Sensor
  * Muhammet Furkan Yalcin
